// Logisim project cpu.circ as structural Verilog: 9 circuits, main circuit cpu
module cpu (
);

  wire alu_1_equal, and_1_out, and_2_out, CLK, control_unit_1_alusrca, control_unit_1_beq,
       control_unit_1_bnq, control_unit_1_irwrite, control_unit_1_lord, control_unit_1_memread,
       control_unit_1_memtoreg, control_unit_1_memwrite, control_unit_1_pcsrc, control_unit_1_pcwrite,
       control_unit_1_regdst, control_unit_1_regwrite, not_1_out, or_1_out, RST;
  wire [1:0] control_unit_1_alusrcb;
  wire [3:0] control_unit_1_alucontrol;
  wire [4:0] multiplexer_2_out;
  wire [15:0] \总周期数 , \无条件分支指令数 , \有条件分支成功跳转 , \有条件分支指令数 ;
  wire [31:0] alu_1_result, bit_extender_1_out, instr_data_memory_1_dout, multiplexer_1_out,
       multiplexer_3_out, multiplexer_4_out, multiplexer_5_out, multiplexer_6_out, register_1_q,
       register_2_q, register_3_q, register_4_aout, register_4_bout, register_5_q, register_file_1_rd1,
       register_file_1_rd2, shifter_1_out, SyscallOut;

  Button \u_总复位  (.out(RST));
  Register_part #(.width(32)) register_1 (
    .D(multiplexer_6_out), .en(or_1_out), .Q(register_1_q), .clk(CLK));  // open: clr
  Hex_Digit_Display hex_digit_display_1 (.value(SyscallOut[27:24]));  // open: dp
  Hex_Digit_Display hex_digit_display_2 (.value(SyscallOut[31:28]));  // open: dp
  Multiplexer #(.width(32), .enable("false")) multiplexer_1 (
    .in0(register_1_q), .in1(register_5_q), .out(multiplexer_1_out), .sel(control_unit_1_lord));
  Hex_Digit_Display hex_digit_display_3 (.value(SyscallOut[19:16]));  // open: dp
  Hex_Digit_Display hex_digit_display_4 (.value(SyscallOut[23:20]));  // open: dp
  Hex_Digit_Display hex_digit_display_5 (.value(SyscallOut[11:8]));  // open: dp
  Hex_Digit_Display hex_digit_display_6 (.value(SyscallOut[15:12]));  // open: dp
  Instr_Data_Memory instr_data_memory_1 (
    .Addr(multiplexer_1_out[25:2]), .Din(register_4_bout), .Dout(instr_data_memory_1_dout),
    .Memwrite(control_unit_1_memwrite), .CLK(CLK), .MemRead(control_unit_1_memread));
  Hex_Digit_Display hex_digit_display_7 (.value(SyscallOut[3:0]));  // open: dp
  Hex_Digit_Display hex_digit_display_8 (.value(SyscallOut[7:4]));  // open: dp
  Register_part #(.width(32)) register_2 (
    .D(instr_data_memory_1_dout), .en(control_unit_1_irwrite), .Q(register_2_q), .clk(CLK));  // open: clr
  Register_part #(.width(32)) register_3 (
    .D(instr_data_memory_1_dout), .en(1'b1), .Q(register_3_q), .clk(CLK));  // open: clr
  // Probe on \总周期数 
  // Probe on \无条件分支指令数 
  // Probe on \有条件分支指令数 
  // Probe on \有条件分支成功跳转 
  Control_Unit control_unit_1 (
    .Op(register_2_q[31:26]), .Funct(register_2_q[5:0]), .lorD(control_unit_1_lord),
    .IRWrite(control_unit_1_irwrite), .PCWrite(control_unit_1_pcwrite), .PCSrc(control_unit_1_pcsrc),
    .ALUControl(control_unit_1_alucontrol), .ALUSrcB(control_unit_1_alusrcb),
    .ALUSrcA(control_unit_1_alusrca), .RegWrite(control_unit_1_regwrite), .CLK(CLK),
    .RegDst(control_unit_1_regdst), .MemtoReg(control_unit_1_memtoreg), .bnq(control_unit_1_bnq),
    .MemWrite(control_unit_1_memwrite), .MemRead(control_unit_1_memread), .beq(control_unit_1_beq));
  Multiplexer #(.width(5), .enable("false")) multiplexer_2 (
    .in0(register_2_q[20:16]), .in1(register_2_q[15:11]), .out(multiplexer_2_out), .sel(control_unit_1_regdst));
  Multiplexer #(.width(32), .enable("false")) multiplexer_3 (
    .in0(register_5_q), .in1(register_3_q), .out(multiplexer_3_out), .sel(control_unit_1_memtoreg));
  Clock clock_1 (.out(CLK));
  Register_File register_file_1 (
    .RD1(register_file_1_rd1), .Din(multiplexer_3_out), .RD2(register_file_1_rd2),
    .WE(control_unit_1_regwrite), .rA(register_2_q[25:21]), .rB(register_2_q[20:16]), .rW(multiplexer_2_out),
    .in_2(CLK));
  assign bit_extender_1_out = {{16{register_2_q[15]}}, register_2_q[15:0]};  // Bit_Extender bit_extender_1
  Register register_4 (
    .A(register_file_1_rd1), .B(register_file_1_rd2), .Aout(register_4_aout), .CLK(CLK),
    .Bout(register_4_bout));
  Multiplexer #(.width(32), .enable("false")) multiplexer_4 (
    .in0(register_1_q), .in1(register_4_aout), .out(multiplexer_4_out), .sel(control_unit_1_alusrca));
  Shifter #(.width(32)) shifter_1 (.in(bit_extender_1_out), .\dist (5'b00010), .out(shifter_1_out));
  Multiplexer #(.select(2), .width(32), .enable("false")) multiplexer_5 (
    .in0(register_4_bout), .in1(32'h4), .in2(bit_extender_1_out), .in3(shifter_1_out),
    .out(multiplexer_5_out), .sel(control_unit_1_alusrcb));
  ALU alu_1 (
    .AluOP(control_unit_1_alucontrol), .X(multiplexer_4_out), .Equal(alu_1_equal), .Result(alu_1_result),
    .Y(multiplexer_5_out));  // open: Signed_Overflow, Result_2, UnSigned_Overflow
  ROM rom_1 ();  // open: addr, data, sel
  not not_1 (not_1_out, alu_1_equal);
  and and_1 (and_1_out, control_unit_1_beq, alu_1_equal);
  and and_2 (and_2_out, control_unit_1_bnq, not_1_out);
  Register_part #(.width(32)) register_5 (.D(alu_1_result), .en(1'b1), .Q(register_5_q), .clk(CLK));  // open: clr
  or or_1 (or_1_out, control_unit_1_pcwrite, and_2_out, and_1_out);
  Multiplexer #(.width(32), .enable("false")) multiplexer_6 (
    .in0(alu_1_result), .in1(register_5_q), .out(multiplexer_6_out), .sel(control_unit_1_pcsrc));
  ROM rom_2 ();  // open: addr, data, sel

  // Notes on the sheet:
  //   数码管输出应该用寄存器锁存，否则显示数据只能一闪而过
  //   可以通过项目增加Logisim库的方式将前几次实验完成的电路作为子电路引入到本电路中使用
  //   数码管输出
  //   总复位信号应将除ROM以外所有存储组件全部清零
endmodule

module pipline (
);

  wire IR1, IR2, IR3, RST, W1, W2, W3;
  wire [15:0] \load_use次数 , \总周期数 , \插入气泡数 , \无条件分支指令数 , \有条件分支成功跳转 ;
  wire [31:0] SyscallOut;

  Button \u_总复位  (.out(RST));
  Button _1 (.out(IR1));
  Button _2 (.out(IR2));
  Button _3 (.out(IR3));
  LED led_1 (.in(W1));
  LED led_2 (.in(W2));
  LED led_3 (.in(W3));
  Hex_Digit_Display hex_digit_display_1 (.value(SyscallOut[31:28]));  // open: dp
  Hex_Digit_Display hex_digit_display_2 (.value(SyscallOut[23:20]));  // open: dp
  Hex_Digit_Display hex_digit_display_3 (.value(SyscallOut[27:24]));  // open: dp
  Hex_Digit_Display hex_digit_display_4 (.value(SyscallOut[19:16]));  // open: dp
  Hex_Digit_Display hex_digit_display_5 (.value(SyscallOut[15:12]));  // open: dp
  Hex_Digit_Display hex_digit_display_6 (.value(SyscallOut[7:4]));  // open: dp
  Hex_Digit_Display hex_digit_display_7 (.value(SyscallOut[11:8]));  // open: dp
  Hex_Digit_Display hex_digit_display_8 (.value(SyscallOut[3:0]));  // open: dp
  // Probe on \总周期数 
  // Probe on \无条件分支指令数 
  // Probe on \有条件分支成功跳转 
  // Probe on \load_use次数 
  // Probe on \插入气泡数 

  // Notes on the sheet:
  //   中断源
  //   中断等待指示
  //   数码管输出
endmodule

module Register_File (
  input  [31:0] Din,
  input  in_2,
  input  WE,
  input  [4:0] rA,
  input  [4:0] rB,
  input  [4:0] rW,
  output [31:0] RD1,
  output [31:0] RD2
);

  // RegisterFile registerfile_1: pin names not known; wires that end beside it: Din, in_2, WE, rW, rA, rB, RD1, RD2

  // Notes on the sheet:
  //   寄存器文件
endmodule

module Instr_Data_Memory (
  input  [23:0] Addr,
  input  [31:0] Din,
  input  Memwrite,
  input  MemRead,
  input  CLK,
  output [31:0] Dout
);

  // MIPS_RAM mips_ram_1: pin names not known; wires that end beside it: Addr, Din, Memwrite, CLK, MemRead, Dout
endmodule

module Register (
  input  [31:0] A,
  input  CLK,
  input  [31:0] B,
  output [31:0] Aout,
  output [31:0] Bout
);

  Register_part #(.width(32)) register_1 (.D(A), .en(1'b1), .Q(Aout), .clk(CLK));  // open: clr
  Register_part #(.width(32)) register_2 (.D(B), .en(1'b1), .Q(Bout), .clk(CLK));  // open: clr
endmodule

module Control_Unit (
  input  [5:0] Op,
  input  [5:0] Funct,
  input  CLK,
  output lorD,
  output PCSrc,
  output ALUSrcA,
  output [1:0] ALUSrcB,
  output RegDst,
  output IRWrite,
  output PCWrite,
  output MemWrite,
  output beq,
  output bnq,
  output MemtoReg,
  output RegWrite,
  output MemRead,
  output [3:0] ALUControl
);

  wire [1:0] ALUop;
  wire [3:0] register_1_q, rom_1_data, \地址转移逻辑_1_adr ;
  wire [4:4] rom_1_data_2;

  \地址转移逻辑  \u_地址转移逻辑_1  (.OP(Op), .FUNC(Funct), .NexAdr(rom_1_data), .Adr(\地址转移逻辑_1_adr ), .P(rom_1_data_2[4]));
  Register_part #(.width(4)) register_1 (.D(\地址转移逻辑_1_adr ), .en(1'b1), .Q(register_1_q), .clk(CLK));  // open: clr
  ALU_Control alu_control_1 (.ALUOP(ALUop), .Func(Funct), .ALU_Control(ALUControl));
  ROM #(.addrWidth(4), .dataWidth(21)) rom_1 (
    .addr(register_1_q),
    .data({lorD, PCSrc, ALUSrcA, ALUSrcB, MemtoReg, RegDst, IRWrite, PCWrite, RegWrite, MemWrite, MemRead, beq, bnq, ALUop, rom_1_data_2[4], rom_1_data}));  // open: sel

  // Notes on the sheet:
  //   contents of rom_1 (hex, n*v repeats v):
  //   13201 30010 60003 100204 8800 60006 100400 40048 4800 c0120 c00a0 6000c 800 d
endmodule

module \地址转移逻辑  (
  input  [5:0] OP,
  input  [5:0] FUNC,
  input  [3:0] NexAdr,
  input  P,
  output [3:0] Adr
);

  wire addi, beq, bnq, comparator_1_eq, comparator_2_eq, lw, not_1_out, R, rw, syscall;
  wire [3:0] \状态_1_y0 ;

  Comparator #(.width(6), .mode("unsigned")) comparator_1 (
    .a(OP), .b({6{1'b0}}), .eq(comparator_1_eq));  // open: gt, lt
  Comparator #(.width(6), .mode("unsigned")) comparator_2 (
    .a(FUNC), .b(6'b001100), .eq(comparator_2_eq));  // open: gt, lt
  Comparator #(.width(6), .mode("unsigned")) comparator_3 (.a(OP), .b(6'b000100), .eq(beq));  // open: gt, lt
  Comparator #(.width(6), .mode("unsigned")) comparator_4 (.a(OP), .b(6'b000101), .eq(bnq));  // open: gt, lt
  Comparator #(.width(6), .mode("unsigned")) comparator_5 (.a(OP), .b(6'b001000), .eq(addi));  // open: gt, lt
  Comparator #(.width(6), .mode("unsigned")) comparator_6 (.a(OP), .b(6'b100011), .eq(lw));  // open: gt, lt
  Comparator #(.width(6), .mode("unsigned")) comparator_7 (.a(OP), .b(6'b101011), .eq(rw));  // open: gt, lt
  not not_1 (not_1_out, comparator_2_eq);
  and and_1 (syscall, comparator_1_eq, comparator_2_eq);
  and and_2 (R, comparator_1_eq, not_1_out);
  \状态  \u_状态_1  (
    .syscall(syscall), .Y3(\状态_1_y0 [3]), .R(R), .beq(beq), .Y2(\状态_1_y0 [2]), .bnq(bnq), .addi(addi),
    .lw(lw), .sw(rw), .Y1(\状态_1_y0 [1]), .Y0(\状态_1_y0 [0]));
  Multiplexer #(.width(4), .enable("false")) multiplexer_1 (.in0(NexAdr), .in1(\状态_1_y0 ), .out(Adr), .sel(P));
endmodule

module \状态  (
  input  syscall,
  input  R,
  input  beq,
  input  bnq,
  input  addi,
  input  lw,
  input  sw,
  output Y3,
  output Y2,
  output Y1,
  output Y0
);

  wire and_1_out, and_2_out, and_3_out, and_4_out, and_5_out, and_6_out, and_7_out, and_10_out, and_11_out,
       and_12_out, and_13_out, and_14_out, and_15_out, and_16_out, and_17_out, and_18_out, and_19_out,
       and_20_out, and_21_out, and_22_out, not_1_out, not_2_out, not_3_out, not_4_out, not_5_out, not_6_out,
       not_7_out, not_8_out, not_9_out, not_10_out, not_11_out, not_12_out, not_13_out, not_14_out,
       not_15_out, not_16_out, not_17_out, not_18_out, not_19_out, not_20_out, not_21_out, not_22_out,
       not_23_out, not_24_out, not_25_out, not_26_out, not_27_out, or_1_out, or_2_out, or_3_out;

  not not_1 (not_1_out, R);
  not not_2 (not_2_out, lw);
  not not_3 (not_3_out, beq);
  not not_4 (not_4_out, bnq);
  not not_5 (not_5_out, addi);
  not not_6 (not_6_out, lw);
  not not_7 (not_7_out, syscall);
  not not_8 (not_8_out, beq);
  not not_9 (not_9_out, beq);
  not not_10 (not_10_out, R);
  not not_11 (not_11_out, beq);
  not not_12 (not_12_out, addi);
  not not_13 (not_13_out, lw);
  and and_1 (and_1_out, not_1_out, not_2_out);
  not not_14 (not_14_out, sw);
  and and_2 (and_2_out, not_3_out, not_4_out);
  and and_3 (and_3_out, not_5_out, not_6_out);
  and and_4 (and_4_out, not_7_out, not_8_out);
  not not_15 (not_15_out, sw);
  and and_5 (and_5_out, not_9_out, lw);
  not not_16 (not_16_out, sw);
  not not_17 (not_17_out, beq);
  not not_18 (not_18_out, beq);
  not not_19 (not_19_out, beq);
  not not_20 (not_20_out, syscall);
  not not_21 (not_21_out, bnq);
  and and_6 (and_6_out, not_10_out, not_11_out);
  not not_22 (not_22_out, bnq);
  and and_7 (and_7_out, not_12_out, not_13_out);
  not not_23 (not_23_out, sw);
  and and_8 (Y3, and_1_out, not_14_out);
  and and_9 (Y2, and_2_out, and_3_out);
  and and_10 (and_10_out, and_4_out, not_15_out);
  and and_11 (and_11_out, and_5_out, not_16_out);
  and and_12 (and_12_out, not_17_out, addi);
  not not_24 (not_24_out, sw);
  and and_13 (and_13_out, not_18_out, bnq);
  not not_25 (not_25_out, sw);
  and and_14 (and_14_out, R, not_19_out);
  not not_26 (not_26_out, sw);
  and and_15 (and_15_out, not_20_out, not_21_out);
  not not_27 (not_27_out, lw);
  and and_16 (and_16_out, and_6_out, not_22_out);
  and and_17 (and_17_out, and_7_out, not_23_out);
  or or_1 (or_1_out, and_10_out, and_11_out);
  and and_18 (and_18_out, and_12_out, not_24_out);
  and and_19 (and_19_out, and_13_out, not_25_out);
  and and_20 (and_20_out, and_14_out, not_26_out);
  and and_21 (and_21_out, and_15_out, not_27_out);
  and and_22 (and_22_out, and_16_out, and_17_out);
  or or_2 (or_2_out, or_1_out, and_18_out);
  or or_3 (or_3_out, and_19_out, and_20_out);
  or or_4 (Y0, and_21_out, and_22_out);
  or or_5 (Y1, or_2_out, or_3_out);
endmodule

module ALU_Control (
  input  [1:0] ALUOP,
  input  [5:0] Func,
  output [3:0] ALU_Control
);

  wire and_1_out, and_2_out, and_3_out, not_1_out, not_2_out, not_3_out, not_4_out;

  not not_1 (not_1_out, ALUOP[0]);
  not not_2 (not_2_out, Func[0]);
  not not_3 (not_3_out, Func[2]);
  not not_4 (not_4_out, Func[4]);
  and and_1 (and_1_out, not_1_out, ALUOP[1]);
  and and_2 (and_2_out, not_2_out, Func[1], not_3_out, Func[3], not_4_out, Func[5]);
  and and_3 (and_3_out, and_1_out, and_2_out);
  Multiplexer #(.width(4), .enable("false")) multiplexer_1 (
    .in0(4'b0101), .in1(4'b1011), .out(ALU_Control), .sel(and_3_out));
endmodule
