// Logisim project cpu.circ as structural Verilog: 12 circuits, main circuit cpu
module cpu (
);

  wire alu_1_equal, and_1_out, bne_beq_1_y, Clock, control_unit_1_alusrca, control_unit_1_branch,
       control_unit_1_iord, control_unit_1_irwrite, control_unit_1_memread, control_unit_1_memtoreg,
       control_unit_1_memwrite, control_unit_1_pcwrite, control_unit_1_regdst, control_unit_1_regwrite,
       or_1_out, RST;
  wire [1:0] control_unit_1_aluop, control_unit_1_alusrcb, control_unit_1_pcsrc;
  wire [3:0] alu_control_1_alucontrol, decoder_1_out_2, PC_q_3;
  wire [4:0] IR_q_2, IR_q_3, multiplexer_2_out;
  wire [5:0] IR_q_4;
  wire [15:0] IR_q, \总周期数 , \无条件分支指令数 , \有条件分支成功跳转 , \有条件分支指令数 ;
  wire [19:0] multiplexer_1_out, PC_q;
  wire [27:0] shifter_1_out;
  wire [27:20] PC_q_2;
  wire [31:0] A_q, alu_1_result, B_q, bit_extender_1_out, C_q, DR_q, instr_data_memory_1_out_6,
       multiplexer_3_out, multiplexer_4_out, multiplexer_5_out, multiplexer_6_out, register_file_1_out_7,
       register_file_1_out_8, SyscallOut;

  Register #(.width(32)) PC (.D(multiplexer_6_out), .en(or_1_out), .Q({PC_q_3, PC_q_2, PC_q}), .clk(Clock), .clr(RST));
  Hex_Digit_Display hex_digit_display_1 (.value(SyscallOut[27:24]));  // open: dp
  Hex_Digit_Display hex_digit_display_2 (.value(SyscallOut[31:28]));  // open: dp
  or or_1 (or_1_out, and_1_out, control_unit_1_pcwrite);
  Multiplexer #(.width(20), .enable("false")) multiplexer_1 (
    .in0(PC_q), .in1(C_q[21:2]), .out(multiplexer_1_out), .sel(control_unit_1_iord));
  Hex_Digit_Display hex_digit_display_3 (.value(SyscallOut[23:20]));  // open: dp
  Hex_Digit_Display hex_digit_display_4 (.value(SyscallOut[19:16]));  // open: dp
  and and_1 (and_1_out, bne_beq_1_y, control_unit_1_branch);
  Instr_Data_Memory instr_data_memory_1 (
    .Adr(multiplexer_1_out), .MemWrite(control_unit_1_memwrite), .Clock(Clock), .Din(B_q),
    .MemRead(control_unit_1_memread), .out_6(instr_data_memory_1_out_6));
  Hex_Digit_Display hex_digit_display_5 (.value(SyscallOut[15:12]));  // open: dp
  Hex_Digit_Display hex_digit_display_6 (.value(SyscallOut[11:8]));  // open: dp
  Control_Unit control_unit_1 (
    .IorD(control_unit_1_iord), .IRWrite(control_unit_1_irwrite), .PCWrite(control_unit_1_pcwrite),
    .PCSrc(control_unit_1_pcsrc), .ALUOp(control_unit_1_aluop), .ALUSrcB(control_unit_1_alusrcb),
    .ALUSrcA(control_unit_1_alusrca), .in_3({IR_q_4, IR_q_3, IR_q_2, IR_q}), .Clock(Clock), .RST(RST),
    .MemRead(control_unit_1_memread), .RegDst(control_unit_1_regdst), .RegWrite(control_unit_1_regwrite),
    .MemtoReg(control_unit_1_memtoreg), .MemWrite(control_unit_1_memwrite), .Branch(control_unit_1_branch));
  Register #(.width(32)) IR (
    .D(instr_data_memory_1_out_6), .en(control_unit_1_irwrite), .Q({IR_q_4, IR_q_3, IR_q_2, IR_q}),
    .clk(Clock), .clr(RST));
  Register #(.width(32)) DR (.D(instr_data_memory_1_out_6), .Q(DR_q), .clk(Clock), .clr(RST));  // open: en
  Hex_Digit_Display hex_digit_display_7 (.value(SyscallOut[3:0]));  // open: dp
  Hex_Digit_Display hex_digit_display_8 (.value(SyscallOut[7:4]));  // open: dp
  Multiplexer #(.width(5), .enable("false")) multiplexer_2 (
    .in0(IR_q_2), .in1(IR_q[15:11]), .out(multiplexer_2_out), .sel(control_unit_1_regdst));
  Multiplexer #(.width(32), .enable("false")) multiplexer_3 (
    .in0(C_q), .in1(DR_q), .out(multiplexer_3_out), .sel(control_unit_1_memtoreg));
  // Probe on control_unit_1_pcsrc
  // Probe on control_unit_1_aluop
  // Probe on control_unit_1_alusrcb
  register_file register_file_1 (
    .Din(multiplexer_3_out), .WE(control_unit_1_regwrite), .W_num(multiplexer_2_out), .R1_num(IR_q_3),
    .R2_num(IR_q_2), .in_2(Clock), .out_7(register_file_1_out_7), .out_8(register_file_1_out_8));
  assign bit_extender_1_out = {{16{IR_q[15]}}, IR_q};  // Bit_Extender bit_extender_1
  // Probe on \总周期数 
  // Probe on \无条件分支指令数 
  // Probe on \有条件分支指令数 
  // Probe on \有条件分支成功跳转 
  Shifter #(.width(28)) shifter_1 (.in({2'b00, IR_q_3, IR_q_2, IR_q}), .\dist (5'b00010), .out(shifter_1_out));
  Register #(.width(32)) A (.D(register_file_1_out_7), .Q(A_q), .clk(Clock), .clr(RST));  // open: en
  Register #(.width(32)) B (.D(register_file_1_out_8), .Q(B_q), .clk(Clock), .clr(RST));  // open: en
  Multiplexer #(.width(32), .enable("false")) multiplexer_4 (
    .in0({PC_q_3, PC_q_2, PC_q}), .in1(A_q), .out(multiplexer_4_out), .sel(control_unit_1_alusrca));
  Button \u_总复位  (.out(RST));
  Clock clock_1 (.out(Clock));
  BNE_BEQ bne_beq_1 (
    .Equal(alu_1_equal), .A(decoder_1_out_2[2]), .Y(bne_beq_1_y), .B(decoder_1_out_2[1]),
    .C(decoder_1_out_2[0]));
  ALU alu_1 (
    .AluOP(alu_control_1_alucontrol), .X(multiplexer_4_out), .Equal(alu_1_equal), .Result(alu_1_result),
    .Y(multiplexer_5_out));  // open: Signed_Overflow, Result_2, UnSigned_Overflow
  Multiplexer #(.select(2), .width(32), .enable("false")) multiplexer_5 (
    .in0(B_q), .in1(32'h1), .in2(bit_extender_1_out), .in3(bit_extender_1_out), .out(multiplexer_5_out),
    .sel(control_unit_1_alusrcb));
  Register #(.width(32)) C (.D(alu_1_result), .Q(C_q), .clk(Clock), .clr(RST));  // open: en
  ALU_Control alu_control_1 (
    .in_1({IR_q_4, IR_q_3, IR_q_2, IR_q}), .ALUControl(alu_control_1_alucontrol), .AluOp(control_unit_1_aluop));
  Multiplexer #(.select(2), .width(32), .enable("false")) multiplexer_6 (
    .in0({PC_q_3, shifter_1_out}), .in1(alu_1_result), .in2(C_q), .out(multiplexer_6_out),
    .sel(control_unit_1_pcsrc));  // open: in3
  Decoder decoder_1 (.in_1({IR_q_4, IR_q_3, IR_q_2, IR_q}), .out_2(decoder_1_out_2));

  // Notes on the sheet:
  //   数码管输出应该用寄存器锁存，否则显示数据只能一闪而过
  //   可以通过项目增加Logisim库的方式将前几次实验完成的电路作为子电路引入到本电路中使用
  //   数码管输出
  //   总复位信号应将除ROM以外所有存储组件全部清零
endmodule

module pipline (
);

  wire IR1, IR2, IR3, RST, W1, W2, W3;
  wire [15:0] \load_use次数 , \总周期数 , \插入气泡数 , \无条件分支指令数 , \有条件分支成功跳转 ;
  wire [31:0] SyscallOut;

  Button \u_总复位  (.out(RST));
  Button _1 (.out(IR1));
  Button _2 (.out(IR2));
  Button _3 (.out(IR3));
  LED led_1 (.in(W1));
  LED led_2 (.in(W2));
  LED led_3 (.in(W3));
  Hex_Digit_Display hex_digit_display_1 (.value(SyscallOut[31:28]));  // open: dp
  Hex_Digit_Display hex_digit_display_2 (.value(SyscallOut[23:20]));  // open: dp
  Hex_Digit_Display hex_digit_display_3 (.value(SyscallOut[27:24]));  // open: dp
  Hex_Digit_Display hex_digit_display_4 (.value(SyscallOut[19:16]));  // open: dp
  Hex_Digit_Display hex_digit_display_5 (.value(SyscallOut[15:12]));  // open: dp
  Hex_Digit_Display hex_digit_display_6 (.value(SyscallOut[11:8]));  // open: dp
  Hex_Digit_Display hex_digit_display_7 (.value(SyscallOut[7:4]));  // open: dp
  Hex_Digit_Display hex_digit_display_8 (.value(SyscallOut[3:0]));  // open: dp
  // Probe on \总周期数 
  // Probe on \无条件分支指令数 
  // Probe on \有条件分支成功跳转 
  // Probe on \load_use次数 
  // Probe on \插入气泡数 

  // Notes on the sheet:
  //   中断源
  //   中断等待指示
  //   数码管输出
endmodule

module register_file (
  input  [31:0] Din,
  input  in_2,
  input  WE,
  input  [4:0] R1_num,
  input  [4:0] R2_num,
  input  [4:0] W_num,
  output [31:0] out_7,
  output [31:0] out_8
);

  // RegisterFile registerfile_1: pin names not known; wires that end beside it: Din, in_2, WE, W_num, R1_num, R2_num, out_7, out_8
endmodule

module Instr_Data_Memory (
  input  [19:0] Adr,
  input  [31:0] Din,
  input  MemWrite,
  input  MemRead,
  input  Clock,
  output [31:0] out_6
);

  // MIPS_RAM mips_ram_1: pin names not known; wires that end beside it: Adr, Din, MemWrite, Clock, MemRead, out_6
endmodule

module Control_Unit (
  input  Clock,
  input  RST,
  input  [31:0] in_3,
  output [1:0] ALUSrcB,
  output [1:0] PCSrc,
  output [1:0] ALUOp,
  output PCWrite,
  output MemRead,
  output IRWrite,
  output IorD,
  output ALUSrcA,
  output RegDst,
  output RegWrite,
  output MemtoReg,
  output MemWrite,
  output Branch
);

  wire \指令_1_y0 , \指令_1_y1 , \指令_1_y2 , \指令_1_y3 ;
  wire [3:0] decoder_1_out_2;

  Decoder decoder_1 (.in_1(in_3), .out_2(decoder_1_out_2));
  \指令  \u_指令_1  (
    .A(decoder_1_out_2[3]), .B(decoder_1_out_2[2]), .C(decoder_1_out_2[1]), .Y0(\指令_1_y0 ),
    .D(decoder_1_out_2[0]), .Y1(\指令_1_y1 ), .Y2(\指令_1_y2 ), .Y3(\指令_1_y3 ), .RST(RST), .in_4(Clock));
  FSM fsm_1 (
    .A(\指令_1_y0 ), .B(\指令_1_y1 ), .C(\指令_1_y2 ), .D(\指令_1_y3 ), .ALUSrcB(ALUSrcB), .PCSrc(PCSrc),
    .ALUOp(ALUOp), .PCWrite(PCWrite), .MemRead(MemRead), .IRWrite(IRWrite), .IorD(IorD), .ALUSrcA(ALUSrcA),
    .RegDst(RegDst), .RegWrite(RegWrite), .MemtoReg(MemtoReg), .MemWrite(MemWrite), .Branch(Branch));
endmodule

module Main_Controller_FSM (
  input  A,
  input  B,
  input  C,
  input  D,
  output _0PCWrite,
  output _1MemRead,
  output _2IRWrite,
  output _3IorD,
  output _4ALUSrcA,
  output _5RegDst,
  output _6RegWrite,
  output _7MemtoReg,
  output _8MemWrite,
  output _9Branch
);

  wire and_1_out, and_2_out, and_3_out, and_4_out, and_6_out, and_7_out, and_9_out, and_10_out, and_11_out,
       and_12_out, and_13_out, and_14_out, and_15_out, not_1_out, not_2_out, not_3_out, not_4_out, not_5_out,
       not_6_out, not_7_out, not_8_out, not_9_out, not_10_out, not_11_out, not_12_out, not_13_out,
       not_14_out, not_15_out, not_16_out, not_17_out, not_18_out, not_19_out, not_20_out, not_21_out,
       not_22_out, not_23_out, not_24_out, not_25_out, not_26_out, not_27_out, not_28_out, not_29_out,
       not_30_out, not_31_out, not_32_out, not_33_out, not_34_out, not_35_out, not_36_out, not_37_out,
       not_38_out, not_39_out;

  not not_1 (not_1_out, A);
  not not_2 (not_2_out, B);
  not not_3 (not_3_out, C);
  not not_4 (not_4_out, D);
  not not_5 (not_5_out, A);
  not not_6 (not_6_out, B);
  not not_7 (not_7_out, C);
  not not_8 (not_8_out, D);
  not not_9 (not_9_out, A);
  not not_10 (not_10_out, B);
  not not_11 (not_11_out, A);
  not not_12 (not_12_out, B);
  not not_13 (not_13_out, C);
  not not_14 (not_14_out, D);
  not not_15 (not_15_out, A);
  not not_16 (not_16_out, C);
  not not_17 (not_17_out, A);
  not not_18 (not_18_out, B);
  not not_19 (not_19_out, A);
  and and_1 (and_1_out, not_19_out, C, not_20_out);
  not not_20 (not_20_out, D);
  not not_21 (not_21_out, C);
  and and_2 (and_2_out, A, not_21_out, D);
  and and_3 (and_3_out, A, not_22_out, not_23_out);
  not not_22 (not_22_out, B);
  not not_23 (not_23_out, C);
  and and_4 (and_4_out, A, not_24_out, D);
  not not_24 (not_24_out, B);
  not not_25 (not_25_out, D);
  not not_26 (not_26_out, A);
  not not_27 (not_27_out, A);
  not not_28 (not_28_out, C);
  not not_29 (not_29_out, D);
  not not_30 (not_30_out, D);
  not not_31 (not_31_out, A);
  not not_32 (not_32_out, A);
  not not_33 (not_33_out, C);
  not not_34 (not_34_out, D);
  not not_35 (not_35_out, A);
  not not_36 (not_36_out, C);
  not not_37 (not_37_out, B);
  not not_38 (not_38_out, C);
  not not_39 (not_39_out, D);
  and and_5 (_0PCWrite, not_1_out, not_2_out, not_3_out, not_4_out);
  and and_6 (and_6_out, not_5_out, not_6_out, not_7_out, not_8_out);
  or or_1 (_1MemRead, and_6_out, and_7_out);
  and and_7 (and_7_out, not_9_out, not_10_out, C, D);
  and and_8 (_2IRWrite, not_11_out, not_12_out, not_13_out, not_14_out);
  and and_9 (and_9_out, not_15_out, B, not_16_out, D);
  or or_2 (_3IorD, and_9_out, and_10_out);
  and and_10 (and_10_out, not_17_out, not_18_out, C, D);
  or or_3 (_4ALUSrcA, and_1_out, and_2_out, and_3_out, and_4_out);
  and and_11 (and_11_out, A, B, C, not_25_out);
  or or_4 (_5RegDst, and_11_out, and_12_out);
  and and_12 (and_12_out, not_26_out, B, C, D);
  and and_13 (and_13_out, not_27_out, B, not_28_out, not_29_out);
  or or_5 (_6RegWrite, and_13_out, and_14_out, and_15_out);
  and and_14 (and_14_out, A, C, not_30_out);
  and and_15 (and_15_out, not_31_out, B, C, D);
  and and_16 (_7MemtoReg, not_32_out, B, not_33_out, not_34_out);
  and and_17 (_8MemWrite, not_35_out, B, not_36_out, D);
  and and_18 (_9Branch, A, not_37_out, not_38_out, not_39_out);
endmodule

module FSM (
  input  A,
  input  B,
  input  C,
  input  D,
  output [1:0] ALUSrcB,
  output [1:0] PCSrc,
  output [1:0] ALUOp,
  output PCWrite,
  output MemRead,
  output IRWrite,
  output IorD,
  output ALUSrcA,
  output RegDst,
  output RegWrite,
  output MemtoReg,
  output MemWrite,
  output Branch
);

  wire and_2_out, and_3_out, and_4_out, and_5_out, and_6_out, and_7_out, and_8_out, and_9_out, and_11_out,
       and_12_out, and_13_out, and_14_out, and_16_out, and_17_out, and_19_out, and_20_out, and_21_out,
       and_22_out, and_23_out, and_24_out, and_25_out, and_28_out, and_29_out, not_1_out, not_2_out,
       not_3_out, not_4_out, not_5_out, not_6_out, not_7_out, not_8_out, not_9_out, not_10_out, not_11_out,
       not_12_out, not_13_out, not_14_out, not_15_out, not_16_out, not_17_out, not_18_out, not_19_out,
       not_20_out, not_21_out, not_22_out, not_23_out, not_24_out, not_25_out, not_26_out, not_27_out,
       not_28_out, not_29_out, not_30_out, not_31_out, not_32_out, not_33_out, not_34_out, not_35_out,
       not_36_out, not_37_out, not_38_out, not_39_out, not_40_out, not_41_out, not_42_out, not_43_out,
       not_44_out, not_45_out, not_46_out, not_47_out, not_48_out, not_49_out, not_50_out, not_51_out,
       not_52_out, not_53_out, not_54_out, not_55_out, not_56_out, not_57_out, not_58_out, not_59_out,
       not_60_out, not_61_out, not_62_out, not_63_out;

  not not_1 (not_1_out, A);
  not not_2 (not_2_out, B);
  not not_3 (not_3_out, D);
  not not_4 (not_4_out, B);
  not not_5 (not_5_out, C);
  not not_6 (not_6_out, A);
  and and_1 (ALUSrcB[0], not_6_out, not_7_out, not_8_out);
  not not_7 (not_7_out, B);
  not not_8 (not_8_out, C);
  not not_9 (not_9_out, B);
  not not_10 (not_10_out, C);
  not not_11 (not_11_out, D);
  not not_12 (not_12_out, B);
  not not_13 (not_13_out, A);
  not not_14 (not_14_out, B);
  not not_15 (not_15_out, C);
  not not_16 (not_16_out, D);
  not not_17 (not_17_out, A);
  not not_18 (not_18_out, D);
  not not_19 (not_19_out, C);
  not not_20 (not_20_out, B);
  not not_21 (not_21_out, C);
  not not_22 (not_22_out, D);
  not not_23 (not_23_out, B);
  not not_24 (not_24_out, A);
  not not_25 (not_25_out, B);
  not not_26 (not_26_out, C);
  not not_27 (not_27_out, D);
  not not_28 (not_28_out, A);
  not not_29 (not_29_out, B);
  not not_30 (not_30_out, C);
  not not_31 (not_31_out, D);
  not not_32 (not_32_out, A);
  not not_33 (not_33_out, B);
  not not_34 (not_34_out, A);
  not not_35 (not_35_out, B);
  not not_36 (not_36_out, C);
  not not_37 (not_37_out, D);
  not not_38 (not_38_out, A);
  not not_39 (not_39_out, C);
  not not_40 (not_40_out, A);
  not not_41 (not_41_out, B);
  not not_42 (not_42_out, A);
  and and_2 (and_2_out, not_42_out, C, not_43_out);
  not not_43 (not_43_out, D);
  not not_44 (not_44_out, C);
  and and_3 (and_3_out, A, not_44_out, D);
  and and_4 (and_4_out, A, not_45_out, not_46_out);
  not not_45 (not_45_out, B);
  not not_46 (not_46_out, C);
  and and_5 (and_5_out, A, not_47_out, D);
  not not_47 (not_47_out, B);
  not not_48 (not_48_out, D);
  not not_49 (not_49_out, A);
  not not_50 (not_50_out, A);
  not not_51 (not_51_out, C);
  not not_52 (not_52_out, D);
  not not_53 (not_53_out, D);
  not not_54 (not_54_out, A);
  not not_55 (not_55_out, A);
  not not_56 (not_56_out, C);
  not not_57 (not_57_out, D);
  not not_58 (not_58_out, A);
  not not_59 (not_59_out, C);
  not not_60 (not_60_out, B);
  not not_61 (not_61_out, C);
  not not_62 (not_62_out, D);
  not not_63 (not_63_out, B);
  and and_6 (and_6_out, not_1_out, not_2_out, C, not_3_out);
  or or_1 (ALUSrcB[1], and_6_out, and_7_out);
  and and_7 (and_7_out, not_4_out, not_5_out, D);
  and and_8 (and_8_out, A, not_9_out, not_10_out, not_11_out);
  or or_2 (PCSrc[1], and_8_out, and_9_out);
  and and_9 (and_9_out, A, not_12_out, C, D);
  and and_10 (PCSrc[0], not_13_out, not_14_out, not_15_out, not_16_out);
  and and_11 (and_11_out, not_17_out, B, C, not_18_out);
  or or_3 (ALUOp[1], and_11_out, and_12_out);
  and and_12 (and_12_out, A, B, not_19_out, D);
  and and_13 (and_13_out, A, not_20_out, not_21_out, not_22_out);
  or or_4 (ALUOp[0], and_13_out, and_14_out);
  and and_14 (and_14_out, A, not_23_out, C, D);
  and and_15 (PCWrite, not_24_out, not_25_out, not_26_out, not_27_out);
  and and_16 (and_16_out, not_28_out, not_29_out, not_30_out, not_31_out);
  or or_5 (MemRead, and_16_out, and_17_out);
  and and_17 (and_17_out, not_32_out, not_33_out, C, D);
  and and_18 (IRWrite, not_34_out, not_35_out, not_36_out, not_37_out);
  and and_19 (and_19_out, not_38_out, B, not_39_out, D);
  or or_6 (IorD, and_19_out, and_20_out);
  and and_20 (and_20_out, not_40_out, not_41_out, C, D);
  or or_7 (ALUSrcA, and_2_out, and_3_out, and_4_out, and_5_out);
  and and_21 (and_21_out, A, B, C, not_48_out);
  or or_8 (RegDst, and_21_out, and_22_out);
  and and_22 (and_22_out, not_49_out, B, C, D);
  and and_23 (and_23_out, not_50_out, B, not_51_out, not_52_out);
  or or_9 (RegWrite, and_23_out, and_24_out, and_25_out);
  and and_24 (and_24_out, A, C, not_53_out);
  and and_25 (and_25_out, not_54_out, B, C, D);
  and and_26 (MemtoReg, not_55_out, B, not_56_out, not_57_out);
  and and_27 (MemWrite, not_58_out, B, not_59_out, D);
  and and_28 (and_28_out, A, not_60_out, not_61_out, not_62_out);
  or or_10 (Branch, and_28_out, and_29_out);
  and and_29 (and_29_out, A, not_63_out, C, D);
endmodule

module Decoder (
  input  [31:0] in_1,
  output [3:0] out_2
);

  wire and_1_out, and_2_out, and_3_out, comparator_1_eq, comparator_2_eq, comparator_3_eq, comparator_4_eq,
       comparator_5_eq, comparator_6_eq, comparator_7_eq, comparator_8_eq, comparator_9_eq, comparator_10_eq;
  wire [3:0] multiplexer_1_out, multiplexer_2_out, multiplexer_3_out, multiplexer_4_out, multiplexer_5_out,
       multiplexer_6_out, multiplexer_7_out, multiplexer_8_out, multiplexer_9_out;

  Comparator #(.width(6)) comparator_1 (.a(in_1[5:0]), .b(6'b100000), .eq(comparator_1_eq));  // open: gt, lt
  Comparator #(.width(6)) comparator_2 (.a(in_1[5:0]), .b(6'b101010), .eq(comparator_2_eq));  // open: gt, lt
  Comparator #(.width(6)) comparator_3 (.a(in_1[5:0]), .b(6'b001100), .eq(comparator_3_eq));  // open: gt, lt
  Comparator #(.width(6)) comparator_4 (.a(in_1[31:26]), .b({6{1'b0}}), .eq(comparator_4_eq));  // open: gt, lt
  Comparator #(.width(6)) comparator_5 (.a(in_1[31:26]), .b(6'b100011), .eq(comparator_5_eq));  // open: gt, lt
  Comparator #(.width(6)) comparator_6 (.a(in_1[31:26]), .b(6'b101011), .eq(comparator_6_eq));  // open: gt, lt
  Comparator #(.width(6)) comparator_7 (.a(in_1[31:26]), .b(6'b000100), .eq(comparator_7_eq));  // open: gt, lt
  Comparator #(.width(6)) comparator_8 (.a(in_1[31:26]), .b(6'b001000), .eq(comparator_8_eq));  // open: gt, lt
  Comparator #(.width(6)) comparator_9 (.a(in_1[31:26]), .b(6'b000101), .eq(comparator_9_eq));  // open: gt, lt
  Comparator #(.width(32)) comparator_10 (.a(in_1), .b({32{1'b0}}), .eq(comparator_10_eq));  // open: gt, lt
  and and_1 (and_1_out, comparator_1_eq, comparator_4_eq);
  and and_2 (and_2_out, comparator_2_eq, comparator_4_eq);
  and and_3 (and_3_out, comparator_3_eq, comparator_4_eq);
  Multiplexer #(.width(4), .enable("false")) multiplexer_1 (
    .in0(4'b0000), .in1(4'b0000), .out(multiplexer_1_out), .sel(and_1_out));
  Multiplexer #(.width(4), .enable("false")) multiplexer_2 (
    .in0(4'b0000), .in1(4'b0010), .out(multiplexer_2_out), .sel(and_2_out));
  Multiplexer #(.width(4), .enable("false")) multiplexer_3 (
    .in0(4'b0000), .in1(4'b0111), .out(multiplexer_3_out), .sel(and_3_out));
  Multiplexer #(.width(4), .enable("false")) multiplexer_4 (
    .in0(4'b0000), .in1(4'b0101), .out(multiplexer_4_out), .sel(comparator_5_eq));
  Multiplexer #(.width(4), .enable("false")) multiplexer_5 (
    .in0(4'b0000), .in1(4'b0110), .out(multiplexer_5_out), .sel(comparator_6_eq));
  Multiplexer #(.width(4), .enable("false")) multiplexer_6 (
    .in0(4'b0000), .in1(4'b0100), .out(multiplexer_6_out), .sel(comparator_7_eq));
  Multiplexer #(.width(4), .enable("false")) multiplexer_7 (
    .in0(4'b0000), .in1(4'b0001), .out(multiplexer_7_out), .sel(comparator_8_eq));
  Multiplexer #(.width(4), .enable("false")) multiplexer_8 (
    .in0(4'b0000), .in1(4'b0011), .out(multiplexer_8_out), .sel(comparator_9_eq));
  Multiplexer #(.width(4), .enable("false")) multiplexer_9 (
    .in0(4'b0000), .in1(4'b1000), .out(multiplexer_9_out), .sel(comparator_10_eq));
  assign out_2 = multiplexer_1_out | multiplexer_2_out | multiplexer_3_out | multiplexer_4_out | multiplexer_5_out | multiplexer_6_out | multiplexer_7_out | multiplexer_8_out | multiplexer_9_out;  // OR_Gate or_1, 4 bits wide
endmodule

module \指令  (
  input  A,
  input  B,
  input  C,
  input  in_4,
  input  D,
  input  RST,
  output Y0,
  output Y1,
  output Y2,
  output Y3
);

  wire and_1_out, and_2_out, and_3_out, and_4_out, and_5_out, and_6_out, and_7_out, and_8_out, and_9_out,
       and_10_out, and_11_out, and_12_out, and_13_out, and_14_out, and_15_out, and_16_out, and_17_out,
       and_18_out, and_19_out, and_20_out, not_1_out, not_2_out, not_3_out, not_4_out, not_5_out, not_6_out,
       not_7_out, not_8_out, not_9_out, not_10_out, not_11_out, not_12_out, not_13_out, not_14_out,
       not_15_out, not_16_out, not_17_out, not_18_out, not_19_out, not_20_out, not_21_out, not_22_out,
       not_23_out, not_24_out, not_25_out, not_26_out, not_27_out, not_28_out, not_29_out, not_30_out,
       not_31_out, not_32_out, not_33_out, not_34_out, not_35_out, not_36_out, not_37_out, not_38_out,
       or_1_out, or_2_out, or_3_out, or_4_out;

  not not_1 (not_1_out, B);
  not not_2 (not_2_out, Y2);
  not not_3 (not_3_out, Y2);
  not not_4 (not_4_out, B);
  not not_5 (not_5_out, Y2);
  not not_6 (not_6_out, C);
  not not_7 (not_7_out, D);
  not not_8 (not_8_out, A);
  not not_9 (not_9_out, B);
  not not_10 (not_10_out, D);
  not not_11 (not_11_out, Y2);
  not not_12 (not_12_out, D);
  not not_13 (not_13_out, Y0);
  not not_14 (not_14_out, Y3);
  not not_15 (not_15_out, B);
  not not_16 (not_16_out, Y2);
  not not_17 (not_17_out, A);
  not not_18 (not_18_out, B);
  not not_19 (not_19_out, C);
  not not_20 (not_20_out, D);
  not not_21 (not_21_out, Y2);
  not not_22 (not_22_out, C);
  not not_23 (not_23_out, Y0);
  not not_24 (not_24_out, Y3);
  not not_25 (not_25_out, Y2);
  not not_26 (not_26_out, D);
  not not_27 (not_27_out, Y1);
  not not_28 (not_28_out, C);
  not not_29 (not_29_out, Y2);
  not not_30 (not_30_out, Y0);
  and and_1 (and_1_out, not_30_out, Y2, not_31_out);
  not not_31 (not_31_out, Y3);
  not not_32 (not_32_out, B);
  and and_2 (and_2_out, not_32_out, C, not_33_out);
  not not_33 (not_33_out, Y0);
  not not_34 (not_34_out, Y0);
  and and_3 (and_3_out, not_34_out, not_35_out, not_36_out);
  not not_35 (not_35_out, Y1);
  not not_36 (not_36_out, Y3);
  not not_37 (not_37_out, B);
  and and_4 (and_4_out, not_37_out, D, not_38_out);
  not not_38 (not_38_out, Y0);
  and and_5 (and_5_out, C, D, Y1);
  and and_6 (and_6_out, not_1_out, D, not_2_out, Y3);
  and and_7 (and_7_out, C, D, not_3_out, Y3);
  and and_8 (and_8_out, not_4_out, C, not_5_out, Y3);
  and and_9 (and_9_out, B, not_6_out, not_7_out, Y3);
  and and_10 (and_10_out, D, Y0, Y1);
  and and_11 (and_11_out, B, Y2, Y3);
  and and_12 (and_12_out, not_8_out, not_9_out, not_10_out, not_11_out, Y3);
  and and_13 (and_13_out, not_12_out, not_13_out, Y2, not_14_out);
  and and_14 (and_14_out, B, C, D, Y3);
  and and_15 (and_15_out, not_15_out, C, D, not_16_out, Y3);
  and and_16 (and_16_out, not_17_out, not_18_out, not_19_out, not_20_out, not_21_out, Y3);
  and and_17 (and_17_out, not_22_out, not_23_out, Y2, not_24_out);
  and and_18 (and_18_out, Y0, not_25_out, Y3);
  and and_19 (and_19_out, B, C, not_26_out, not_27_out, Y3);
  and and_20 (and_20_out, B, not_28_out, D, not_29_out, Y3);
  or or_1 (or_1_out, and_1_out, and_2_out, and_3_out, and_4_out);
  or or_2 (or_2_out, and_5_out, and_6_out, and_7_out, and_8_out, and_9_out);
  or or_3 (or_3_out, and_10_out, and_11_out, and_12_out, and_13_out, and_14_out);
  or or_4 (or_4_out, and_15_out, and_16_out, and_17_out, and_18_out, and_19_out, and_20_out);
  Register #(.width(1)) register_1 (.D(or_2_out), .Q(Y0), .clk(in_4), .clr(RST));  // open: en
  Register #(.width(1)) register_2 (.D(or_3_out), .Q(Y1), .clk(in_4), .clr(RST));  // open: en
  Register #(.width(1)) register_3 (.D(or_4_out), .Q(Y2), .clk(in_4), .clr(RST));  // open: en
  Register #(.width(1)) register_4 (.D(or_1_out), .Q(Y3), .clk(in_4), .clr(RST));  // open: en
endmodule

module ALU_Control (
  input  [31:0] in_1,
  input  [1:0] AluOp,
  output [3:0] ALUControl
);

  wire and_1_out, and_2_out, and_3_out, comparator_1_eq, comparator_2_eq, comparator_3_eq, comparator_4_eq,
       comparator_5_eq, comparator_6_eq;
  wire [3:0] multiplexer_1_out, multiplexer_2_out, multiplexer_3_out, multiplexer_4_out;

  Comparator #(.width(6)) comparator_1 (.a(in_1[5:0]), .b(6'b100000), .eq(comparator_1_eq));  // open: gt, lt
  Comparator #(.width(6)) comparator_2 (.a(in_1[5:0]), .b(6'b101010), .eq(comparator_2_eq));  // open: gt, lt
  Comparator #(.width(6)) comparator_3 (.a(in_1[31:26]), .b({6{1'b0}}), .eq(comparator_3_eq));  // open: gt, lt
  Comparator #(.width(2)) comparator_4 (.a(AluOp), .b(2'b10), .eq(comparator_4_eq));  // open: gt, lt
  Comparator #(.width(2)) comparator_5 (.a(AluOp), .b(2'b01), .eq(comparator_5_eq));  // open: gt, lt
  Comparator #(.width(2)) comparator_6 (.a(AluOp), .b(2'b00), .eq(comparator_6_eq));  // open: gt, lt
  and and_1 (and_1_out, comparator_3_eq, comparator_4_eq);
  and and_2 (and_2_out, comparator_1_eq, and_1_out);
  and and_3 (and_3_out, comparator_2_eq, and_1_out);
  Multiplexer #(.width(4)) multiplexer_1 (
    .in0(4'b0000), .in1(4'b0101), .out(multiplexer_1_out), .sel(and_2_out));  // open: en
  Multiplexer #(.width(4)) multiplexer_2 (
    .in0(4'b0000), .in1(4'b1011), .out(multiplexer_2_out), .sel(and_3_out));  // open: en
  Multiplexer #(.width(4)) multiplexer_3 (
    .in0(4'b0000), .in1(4'b0110), .out(multiplexer_3_out), .sel(comparator_5_eq));  // open: en
  Multiplexer #(.width(4)) multiplexer_4 (
    .in0(4'b0000), .in1(4'b0101), .out(multiplexer_4_out), .sel(comparator_6_eq));  // open: en
  assign ALUControl = multiplexer_1_out | multiplexer_2_out | multiplexer_3_out | multiplexer_4_out;  // OR_Gate or_1, 4 bits wide
endmodule

module Main_Controller (
  input  A,
  input  B,
  input  C,
  input  D,
  output ALUSrcBH,
  output [1:0] ALUSrcB,
  output ALUSrcBL,
  output PCSrcH,
  output [1:0] PCSrc,
  output PCSrcL,
  output ALUOpH,
  output [1:0] ALUOp,
  output ALUOpL
);

  wire and_2_out, and_3_out, and_4_out, and_5_out, and_7_out, and_8_out, and_9_out, and_10_out, not_1_out,
       not_2_out, not_3_out, not_4_out, not_5_out, not_6_out, not_7_out, not_8_out, not_9_out, not_10_out,
       not_11_out, not_12_out, not_13_out, not_14_out, not_15_out, not_16_out, not_17_out, not_18_out,
       not_19_out, not_20_out, not_21_out, not_22_out, not_23_out;

  not not_1 (not_1_out, A);
  not not_2 (not_2_out, B);
  not not_3 (not_3_out, D);
  not not_4 (not_4_out, B);
  not not_5 (not_5_out, C);
  not not_6 (not_6_out, A);
  and and_1 (ALUSrcB[0], not_6_out, not_7_out, not_8_out);
  not not_7 (not_7_out, B);
  not not_8 (not_8_out, C);
  not not_9 (not_9_out, B);
  not not_10 (not_10_out, C);
  not not_11 (not_11_out, D);
  not not_12 (not_12_out, B);
  not not_13 (not_13_out, A);
  not not_14 (not_14_out, B);
  not not_15 (not_15_out, C);
  not not_16 (not_16_out, D);
  not not_17 (not_17_out, A);
  not not_18 (not_18_out, D);
  not not_19 (not_19_out, C);
  not not_20 (not_20_out, B);
  not not_21 (not_21_out, C);
  not not_22 (not_22_out, D);
  not not_23 (not_23_out, B);
  and and_2 (and_2_out, not_1_out, not_2_out, C, not_3_out);
  or or_1 (ALUSrcB[1], and_2_out, and_3_out);
  and and_3 (and_3_out, not_4_out, not_5_out, D);
  and and_4 (and_4_out, A, not_9_out, not_10_out, not_11_out);
  or or_2 (PCSrc[1], and_4_out, and_5_out);
  and and_5 (and_5_out, A, not_12_out, C, D);
  and and_6 (PCSrc[0], not_13_out, not_14_out, not_15_out, not_16_out);
  and and_7 (and_7_out, not_17_out, B, C, not_18_out);
  or or_3 (ALUOp[1], and_7_out, and_8_out);
  and and_8 (and_8_out, A, B, not_19_out, D);
  and and_9 (and_9_out, A, not_20_out, not_21_out, not_22_out);
  or or_4 (ALUOp[0], and_9_out, and_10_out);
  and and_10 (and_10_out, A, not_23_out, C, D);

  assign ALUOpH = ALUOp[1];
  assign ALUOpL = ALUOp[0];
  assign ALUSrcBH = ALUSrcB[1];
  assign ALUSrcBL = ALUSrcB[0];
  assign PCSrcH = PCSrc[1];
  assign PCSrcL = PCSrc[0];
endmodule

module BNE_BEQ (
  input  Equal,
  input  A,
  input  B,
  input  C,
  output Y
);

  wire and_1_out, and_2_out, and_3_out, and_4_out, and_5_out, and_6_out, not_1_out, not_2_out, not_3_out,
       not_4_out;

  not not_1 (not_1_out, Equal);
  and and_1 (and_1_out, not_1_out, not_2_out);
  not not_2 (not_2_out, A);
  and and_2 (and_2_out, B, C);
  and and_3 (and_3_out, Equal, A);
  not not_3 (not_3_out, B);
  and and_4 (and_4_out, not_3_out, not_4_out);
  not not_4 (not_4_out, C);
  and and_5 (and_5_out, and_1_out, and_2_out);
  and and_6 (and_6_out, and_3_out, and_4_out);
  or or_1 (Y, and_5_out, and_6_out);
endmodule
