// Logisim project project.circ as structural Verilog: 7 circuits, main circuit 一位可逆计数器
module \一位可逆计数器  (
  input  A,
  input  B,
  input  C,
  output D,
  output Sum,
  output J
);

  wire and_2_out, and_3_out, and_4_out, and_5_out, not_1_out, not_2_out, not_3_out, not_4_out, not_5_out,
       not_6_out, not_7_out, not_8_out, not_9_out;

  not not_1 (not_1_out, A);
  not not_2 (not_2_out, A);
  not not_3 (not_3_out, B);
  not not_4 (not_4_out, A);
  not not_5 (not_5_out, C);
  not not_6 (not_6_out, B);
  not not_7 (not_7_out, C);
  not not_8 (not_8_out, B);
  not not_9 (not_9_out, C);
  and and_1 (D, not_1_out, B, C);
  and and_2 (and_2_out, not_2_out, not_3_out, C);
  and and_3 (and_3_out, not_4_out, B, not_5_out);
  and and_4 (and_4_out, A, not_6_out, not_7_out);
  and and_5 (and_5_out, A, B, C);
  and and_6 (J, A, not_8_out, not_9_out);
  or or_1 (Sum, and_2_out, and_3_out, and_4_out, and_5_out);
endmodule

module _8421 (
  input  A3,
  input  A2,
  input  A1,
  input  A0,
  output D7,
  output D6,
  output D5,
  output D4,
  output D3,
  output D2,
  output D1,
  output D0
);

  wire and_1_out, and_2_out, and_4_out, and_5_out, and_6_out, and_7_out, not_1_out, not_2_out, not_3_out,
       not_4_out, not_5_out;

  and and_1 (and_1_out, A3, A1);
  and and_2 (and_2_out, A3, A2);
  not not_1 (not_1_out, A2);
  and and_3 (D3, A3, not_1_out, not_2_out);
  not not_2 (not_2_out, A1);
  not not_3 (not_3_out, A3);
  and and_4 (and_4_out, not_3_out, A2);
  and and_5 (and_5_out, A2, A1);
  not not_4 (not_4_out, A3);
  and and_6 (and_6_out, not_4_out, A1);
  and and_7 (and_7_out, A3, A2, not_5_out);
  not not_5 (not_5_out, A1);
  or or_1 (D4, and_1_out, and_2_out);
  or or_2 (D2, and_4_out, and_5_out);
  or or_3 (D1, and_6_out, and_7_out);

  assign D0 = A0;
  assign D5 = 1'b0;
  assign D6 = 1'b0;
  assign D7 = 1'b0;
endmodule

module LCD (
  input  A3,
  input  A2,
  input  A1,
  input  A0,
  output a,
  output b,
  output c,
  output d,
  output e,
  output f,
  output g
);

  wire and_1_out, and_2_out, and_3_out, and_4_out, and_5_out, and_6_out, and_7_out, and_8_out, and_9_out,
       and_10_out, and_11_out, and_12_out, and_13_out, and_14_out, and_15_out, and_16_out, and_17_out,
       and_18_out, and_19_out, and_20_out, and_21_out, and_22_out, and_23_out, and_24_out, and_25_out,
       and_26_out, not_1_out, not_2_out, not_3_out, not_4_out, not_5_out, not_6_out, not_7_out, not_8_out,
       not_9_out, not_10_out, not_11_out, not_12_out, not_13_out, not_14_out, not_15_out, not_16_out,
       not_17_out, not_18_out, not_19_out, not_20_out, not_21_out, not_22_out, not_23_out, not_24_out,
       not_25_out, not_26_out, not_27_out, not_28_out, not_29_out, not_30_out, not_31_out, not_32_out,
       not_33_out, not_34_out, not_35_out, not_36_out, not_37_out, not_38_out, not_39_out, not_40_out,
       not_41_out, not_42_out, not_43_out, not_44_out, not_45_out, not_46_out, not_47_out, not_48_out,
       not_49_out, not_50_out, not_51_out, not_52_out;

  not not_1 (not_1_out, A3);
  not not_2 (not_2_out, A1);
  and and_1 (and_1_out, not_1_out, not_2_out, not_3_out);
  not not_3 (not_3_out, A0);
  not not_4 (not_4_out, A3);
  and and_2 (and_2_out, not_4_out, A2, not_5_out);
  not not_5 (not_5_out, A1);
  not not_6 (not_6_out, A3);
  and and_3 (and_3_out, not_6_out, A2, not_7_out);
  not not_7 (not_7_out, A0);
  not not_8 (not_8_out, A2);
  and and_4 (and_4_out, A3, not_8_out, not_9_out);
  not not_9 (not_9_out, A1);
  not not_10 (not_10_out, A3);
  and and_5 (and_5_out, not_10_out, not_11_out, not_12_out);
  not not_11 (not_11_out, A2);
  not not_12 (not_12_out, A0);
  not not_13 (not_13_out, A3);
  and and_6 (and_6_out, not_13_out, A1);
  not not_14 (not_14_out, A3);
  and and_7 (and_7_out, not_14_out, A2, A0);
  and and_8 (and_8_out, A3, not_15_out, not_16_out);
  not not_15 (not_15_out, A2);
  not not_16 (not_16_out, A1);
  not not_17 (not_17_out, A3);
  and and_9 (and_9_out, not_17_out, not_18_out);
  not not_18 (not_18_out, A2);
  not not_19 (not_19_out, A3);
  not not_20 (not_20_out, A1);
  and and_10 (and_10_out, not_19_out, not_20_out, not_21_out);
  not not_21 (not_21_out, A0);
  not not_22 (not_22_out, A2);
  and and_11 (and_11_out, not_22_out, not_23_out);
  not not_23 (not_23_out, A1);
  not not_24 (not_24_out, A3);
  and and_12 (and_12_out, not_24_out, A1, A0);
  not not_25 (not_25_out, A3);
  not not_26 (not_26_out, A2);
  and and_13 (and_13_out, not_25_out, not_26_out, A1);
  not not_27 (not_27_out, A3);
  and and_14 (and_14_out, not_27_out, A2, not_28_out);
  not not_28 (not_28_out, A1);
  not not_29 (not_29_out, A3);
  and and_15 (and_15_out, not_29_out, A2, not_30_out);
  not not_30 (not_30_out, A0);
  and and_16 (and_16_out, A3, not_31_out, not_32_out);
  not not_31 (not_31_out, A2);
  not not_32 (not_32_out, A1);
  not not_33 (not_33_out, A2);
  not not_34 (not_34_out, A1);
  and and_17 (and_17_out, not_33_out, not_34_out, not_35_out);
  not not_35 (not_35_out, A0);
  not not_36 (not_36_out, A3);
  and and_18 (and_18_out, not_36_out, A1, not_37_out);
  not not_37 (not_37_out, A0);
  not not_38 (not_38_out, A3);
  not not_39 (not_39_out, A2);
  not not_40 (not_40_out, A0);
  not not_41 (not_41_out, A3);
  not not_42 (not_42_out, A2);
  not not_43 (not_43_out, A3);
  not not_44 (not_44_out, A0);
  not not_45 (not_45_out, A3);
  not not_46 (not_46_out, A1);
  not not_47 (not_47_out, A2);
  not not_48 (not_48_out, A1);
  not not_49 (not_49_out, A2);
  and and_19 (and_19_out, not_49_out, not_50_out);
  not not_50 (not_50_out, A1);
  not not_51 (not_51_out, A3);
  and and_20 (and_20_out, not_51_out, A0);
  not not_52 (not_52_out, A3);
  and and_21 (and_21_out, not_52_out, A2);
  or or_1 (a, and_1_out, and_2_out, and_3_out, and_4_out);
  or or_2 (b, and_5_out, and_6_out, and_7_out, and_8_out);
  or or_3 (c, and_9_out, and_10_out, and_11_out, and_12_out);
  or or_4 (d, and_13_out, and_14_out, and_15_out, and_16_out);
  or or_5 (e, and_17_out, and_18_out);
  and and_22 (and_22_out, not_38_out, not_39_out, not_40_out);
  and and_23 (and_23_out, not_41_out, not_42_out, A1);
  and and_24 (and_24_out, not_43_out, A1, not_44_out);
  and and_25 (and_25_out, not_45_out, A2, not_46_out, A0);
  and and_26 (and_26_out, A3, not_47_out, not_48_out);
  or or_6 (g, and_19_out, and_20_out, and_21_out);
  or or_7 (f, and_22_out, and_23_out, and_24_out, and_25_out, and_26_out);
endmodule

module \实验室系统  (
  input  cpu,
  input  cpd
);

  wire clr_out, lcd_1_a, lcd_1_b, lcd_1_c, lcd_1_d, lcd_1_e, lcd_1_f, lcd_1_g, lcd_2_a, lcd_2_b, lcd_2_c,
       lcd_2_d, lcd_2_e, lcd_2_f, lcd_2_g, n8421_1_d0, n8421_1_d1, n8421_1_d2, n8421_1_d3, n8421_1_d4,
       n8421_1_d5, n8421_1_d6, n8421_1_d7, \四位可逆计数器_1_qa , \四位可逆计数器_1_qb , \四位可逆计数器_1_qc , \四位可逆计数器_1_qd ,
       \四位可逆计数器_1_报警 ;

  Button clr (.out(clr_out));
  LED led_1 (.in(\四位可逆计数器_1_报警 ));
  \四位可逆计数器  \u_四位可逆计数器_1  (
    .cpu(cpu), .cpd(cpd), .\报警 (\四位可逆计数器_1_报警 ), .clr(clr_out), .Qd(\四位可逆计数器_1_qd ), .Qc(\四位可逆计数器_1_qc ),
    .Qb(\四位可逆计数器_1_qb ), .Qa(\四位可逆计数器_1_qa ));
  _8421 u_8421_1 (
    .A3(\四位可逆计数器_1_qd ), .A2(\四位可逆计数器_1_qc ), .A1(\四位可逆计数器_1_qb ), .A0(\四位可逆计数器_1_qa ), .D7(n8421_1_d7),
    .D6(n8421_1_d6), .D5(n8421_1_d5), .D4(n8421_1_d4), .D3(n8421_1_d3), .D2(n8421_1_d2), .D1(n8421_1_d1),
    .D0(n8421_1_d0));
  LCD lcd_1 (
    .A3(n8421_1_d7), .A2(n8421_1_d6), .A1(n8421_1_d5), .A0(n8421_1_d4), .a(lcd_1_a), .b(lcd_1_b),
    .c(lcd_1_c), .d(lcd_1_d), .e(lcd_1_e), .f(lcd_1_f), .g(lcd_1_g));
  _7_Segment_Display u_7_segment_display_1 (
    .g(lcd_1_d), .f(lcd_1_a), .a(lcd_1_b), .b(lcd_1_c), .e(lcd_1_e), .d(lcd_1_f), .c(lcd_1_g));  // open: dp
  _7_Segment_Display u_7_segment_display_2 (
    .g(lcd_2_d), .f(lcd_2_a), .a(lcd_2_b), .b(lcd_2_c), .e(lcd_2_e), .d(lcd_2_f), .c(lcd_2_g));  // open: dp
  LCD lcd_2 (
    .A3(n8421_1_d3), .A2(n8421_1_d2), .A1(n8421_1_d1), .A0(n8421_1_d0), .a(lcd_2_a), .b(lcd_2_b),
    .c(lcd_2_c), .d(lcd_2_d), .e(lcd_2_e), .f(lcd_2_f), .g(lcd_2_g));
endmodule

module _1 (
  input  cpu,
  input  cpd,
  output cl,
  output key
);

  wire and_1_out, and_2_out, not_2_out, not_3_out;

  not not_1 (cl, cpd);
  not not_2 (not_2_out, cpu);
  not not_3 (not_3_out, cpd);
  and and_1 (and_1_out, not_2_out, cpd);
  and and_2 (and_2_out, cpu, not_3_out);
  or or_1 (key, and_1_out, and_2_out);
endmodule

// 计数器
module \四位可逆计数器  (
  input  clr,
  input  cpu,
  input  cpd,
  output \报警 ,
  output Qd,
  output Qc,
  output Qb,
  output Qa
);

  wire and_1_out, and_3_out, clock_1_out, n1_1_cl, n1_1_key, not_1_out, not_2_out, not_3_out, not_4_out,
       or_1_out, \一位可逆计数器_1_d , \一位可逆计数器_1_j , \一位可逆计数器_1_sum , \一位可逆计数器_2_d , \一位可逆计数器_2_j ,
       \一位可逆计数器_2_sum , \一位可逆计数器_3_d , \一位可逆计数器_3_j , \一位可逆计数器_3_sum , \一位可逆计数器_4_d , \一位可逆计数器_4_sum ;

  _1 u_1_1 (.cpu(cpu), .cpd(cpd), .cl(n1_1_cl), .key(n1_1_key));
  not not_1 (not_1_out, n1_1_cl);
  not not_2 (not_2_out, and_1_out);
  and and_1 (and_1_out, not_1_out, not_3_out);
  not not_3 (not_3_out, or_1_out);
  and and_2 (\报警 , n1_1_cl, \一位可逆计数器_4_d );
  not not_4 (not_4_out, \报警 );
  and and_3 (and_3_out, n1_1_key, not_2_out, not_4_out);
  \一位可逆计数器  \u_一位可逆计数器_1  (
    .A(not_1_out), .B(n1_1_cl), .C(Qa), .D(\一位可逆计数器_1_d ), .Sum(\一位可逆计数器_1_sum ), .J(\一位可逆计数器_1_j ));
  \一位可逆计数器  \u_一位可逆计数器_2  (
    .A(\一位可逆计数器_1_j ), .B(Qb), .C(\一位可逆计数器_1_d ), .D(\一位可逆计数器_2_d ), .Sum(\一位可逆计数器_2_sum ), .J(\一位可逆计数器_2_j ));
  \一位可逆计数器  \u_一位可逆计数器_3  (
    .A(\一位可逆计数器_2_j ), .B(Qc), .C(\一位可逆计数器_2_d ), .D(\一位可逆计数器_3_d ), .Sum(\一位可逆计数器_3_sum ), .J(\一位可逆计数器_3_j ));
  \一位可逆计数器  \u_一位可逆计数器_4  (
    .A(\一位可逆计数器_3_j ), .B(Qd), .C(\一位可逆计数器_3_d ), .D(\一位可逆计数器_4_d ), .Sum(\一位可逆计数器_4_sum ));  // open: J
  Clock clock_1 (.out(clock_1_out));
  D_Flip_Flop d_ff_1 (.clk(clock_1_out), .D(\一位可逆计数器_4_sum ), .Q(Qd), .en(and_3_out), .reset(clr));  // open: Qn, preset
  D_Flip_Flop d_ff_2 (.clk(clock_1_out), .D(\一位可逆计数器_3_sum ), .Q(Qc), .en(and_3_out), .reset(clr));  // open: Qn, preset
  D_Flip_Flop d_ff_3 (.clk(clock_1_out), .D(\一位可逆计数器_2_sum ), .Q(Qb), .en(and_3_out), .reset(clr));  // open: Qn, preset
  D_Flip_Flop d_ff_4 (.clk(clock_1_out), .D(\一位可逆计数器_1_sum ), .Q(Qa), .en(and_3_out), .reset(clr));  // open: Qn, preset
  or or_1 (or_1_out, Qa, Qb, Qc, Qd);
endmodule

module \可逆计数器  (
  input  in_1,
  input  in_2,
  input  in_3,
  output Q0,
  output Q1,
  output Q2,
  output Q3
);

  wire d_ff_1_qn, d_ff_2_qn, d_ff_3_qn, d_ff_4_qn, xor_1_out, xor_2_out, xor_3_out;

  D_Flip_Flop d_ff_1 (.clk(in_1), .D(d_ff_1_qn), .Q(Q0), .Qn(d_ff_1_qn), .reset(in_2));  // open: preset, en
  xor xor_1 (xor_1_out, d_ff_1_qn, in_3);
  D_Flip_Flop d_ff_2 (.clk(xor_1_out), .D(d_ff_2_qn), .Q(Q1), .Qn(d_ff_2_qn), .reset(in_2));  // open: preset, en
  xor xor_2 (xor_2_out, d_ff_2_qn, in_3);
  D_Flip_Flop d_ff_3 (.clk(xor_2_out), .D(d_ff_3_qn), .Q(Q2), .Qn(d_ff_3_qn), .reset(in_2));  // open: preset, en
  xor xor_3 (xor_3_out, d_ff_3_qn, in_3);
  D_Flip_Flop d_ff_4 (.clk(xor_3_out), .D(d_ff_4_qn), .Q(Q3), .Qn(d_ff_4_qn), .reset(in_2));  // open: preset, en
endmodule
