// Logisim project T1-可重叠Mealy.circ as structural Verilog: 1 circuit, main circuit main
module main (
  input  X,
  output Z
);

  wire and_2_out, and_3_out, clock_1_out, D1_q, D1_qn, D2_q, D2_qn, not_1_out, or_1_out;

  Clock clock_1 (.out(clock_1_out));
  D_Flip_Flop D1 (.clk(clock_1_out), .D(and_2_out), .Q(D1_q), .Qn(D1_qn));  // open: preset, en, reset
  not not_1 (not_1_out, X);
  D_Flip_Flop D2 (.clk(clock_1_out), .D(or_1_out), .Q(D2_q), .Qn(D2_qn));  // open: preset, en, reset
  and and_1 (Z, D1_q, D2_qn, X);
  and and_2 (and_2_out, not_1_out, D2_q);
  and and_3 (and_3_out, D1_qn, D2_q);
  or or_1 (or_1_out, and_3_out, X);
endmodule
