// Logisim project T1-可重叠Moore.circ as structural Verilog: 1 circuit, main circuit main
module main (
  input  X,
  output out_2
);

  wire and_1_out, and_2_out, and_3_out, and_4_out, and_5_out, clock_1_out, D1_q, D1_qn, D2_q, D3_q, D3_qn,
       not_1_out, or_1_out;

  not not_1 (not_1_out, X);
  and and_1 (and_1_out, X, D1_qn);
  D_Flip_Flop D1 (.clk(clock_1_out), .D(or_1_out), .Q(D1_q), .Qn(D1_qn));  // open: preset, en, reset
  or or_1 (or_1_out, and_5_out, and_4_out, and_1_out);
  D_Flip_Flop D2 (.clk(clock_1_out), .D(and_2_out), .Q(D2_q));  // open: Qn, preset, en, reset
  and and_2 (and_2_out, X, D1_qn, D3_q);
  D_Flip_Flop D3 (.clk(clock_1_out), .D(and_3_out), .Q(D3_q), .Qn(D3_qn));  // open: preset, en, reset
  and and_3 (and_3_out, D1_q, not_1_out);
  and and_4 (and_4_out, D1_q, D3_qn);
  and and_5 (and_5_out, D3_q, X);
  and and_6 (out_2, D1_q, D2_q, D3_qn);
  Clock clock_1 (.out(clock_1_out));
endmodule
