// Logisim project T2.circ as structural Verilog: 1 circuit, main circuit main
module main (
  input  X,
  output Z
);

  wire and_1_out, and_2_out, and_4_out, and_5_out, and_6_out, clock_1_out, D1_q, D2_q, D2_qn, D3_q, D3_qn,
       not_1_out, not_2_out, or_1_out, or_2_out, xor_1_out, xor_2_out;

  Clock clock_1 (.out(clock_1_out));
  D_Flip_Flop D1 (.clk(clock_1_out), .D(or_2_out), .Q(D1_q));  // open: Qn, preset, en, reset
  D_Flip_Flop D2 (.clk(clock_1_out), .D(or_1_out), .Q(D2_q), .Qn(D2_qn));  // open: preset, en, reset
  D_Flip_Flop D3 (.clk(clock_1_out), .D(and_4_out), .Q(D3_q), .Qn(D3_qn));  // open: preset, en, reset
  not not_1 (not_1_out, X);
  xor xor_1 (xor_1_out, X, D1_q);
  xor xor_2 (xor_2_out, D1_q, X);
  and and_1 (and_1_out, D3_q, not_1_out);
  and and_2 (and_2_out, X, D2_qn);
  and and_3 (Z, xor_1_out, D2_qn, D3_qn);
  not not_2 (not_2_out, xor_2_out);
  and and_4 (and_4_out, not_2_out, D2_q);
  and and_5 (and_5_out, D2_q, D3_q);
  or or_1 (or_1_out, not_2_out, and_5_out);
  and and_6 (and_6_out, D1_q, D2_q, D3_qn);
  or or_2 (or_2_out, and_2_out, and_6_out, and_1_out);
endmodule
