// Logisim project T3-Mealy.circ as structural Verilog: 1 circuit, main circuit main
module main (
  input  X,
  output Z
);

  wire and_1_out, and_2_out, and_3_out, and_4_out, and_5_out, and_6_out, clock_1_out, D1_q, D1_qn, D2_q,
       D2_qn, D3_qn, not_1_out, or_1_out, or_2_out;

  Clock clock_1 (.out(clock_1_out));
  D_Flip_Flop D1 (.clk(clock_1_out), .D(and_4_out), .Q(D1_q), .Qn(D1_qn));  // open: preset, en, reset
  not not_1 (not_1_out, X);
  D_Flip_Flop D2 (.clk(clock_1_out), .D(or_1_out), .Q(D2_q), .Qn(D2_qn));  // open: preset, en, reset
  D_Flip_Flop D3 (.clk(clock_1_out), .D(or_2_out), .Qn(D3_qn));  // open: Q, preset, en, reset
  and and_1 (and_1_out, D1_qn, D2_q, D3_qn);
  and and_2 (and_2_out, not_1_out, D1_qn, D3_qn);
  and and_3 (and_3_out, D2_qn, D1_q);
  and and_4 (and_4_out, D2_qn, X);
  and and_5 (and_5_out, D1_qn, D2_q, D3_qn);
  and and_6 (and_6_out, not_1_out, D1_q, D2_qn);
  or or_1 (or_1_out, and_1_out, and_2_out, and_3_out);
  and and_7 (Z, D1_q, D2_q, D3_qn);
  or or_2 (or_2_out, and_5_out, and_6_out);
endmodule
