// Logisim project T3-Moore.circ as structural Verilog: 1 circuit, main circuit main
module main (
  input  X
);

  wire and_1_out, and_2_out, and_3_out, and_4_out, and_5_out, and_6_out, and_7_out, and_8_out, and_9_out,
       and_10_out, and_11_out, clock_1_out, D1_q, D1_qn, D2_q, D2_qn, D3_q, D3_qn, not_1_out, or_1_out,
       or_2_out, or_3_out;

  not not_1 (not_1_out, X);
  and and_1 (and_1_out, D2_q, D1_qn);
  and and_2 (and_2_out, X, D1_qn);
  and and_3 (and_3_out, X, D3_q);
  and and_4 (and_4_out, D2_qn, D1_q);
  and and_5 (and_5_out, D2_q, D1_qn);
  and and_6 (and_6_out, X, D3_q, D2_qn);
  and and_7 (and_7_out, not_1_out, D2_qn);
  and and_8 (and_8_out, D2_qn, D1_q);
  and and_9 (and_9_out, D2_q, D1_qn);
  and and_10 (and_10_out, not_1_out, D3_q);
  or or_1 (or_1_out, and_1_out, and_2_out, and_3_out);
  or or_2 (or_2_out, and_4_out, and_5_out, and_6_out);
  or or_3 (or_3_out, and_7_out, and_8_out, and_9_out, and_10_out);
  Clock clock_1 (.out(clock_1_out));
  D_Flip_Flop D3 (.clk(clock_1_out), .D(or_1_out), .Q(D3_q), .Qn(D3_qn));  // open: preset, en, reset
  D_Flip_Flop D2 (.clk(clock_1_out), .D(or_2_out), .Q(D2_q), .Qn(D2_qn));  // open: preset, en, reset
  D_Flip_Flop D1 (.clk(clock_1_out), .D(or_3_out), .Q(D1_q), .Qn(D1_qn));  // open: preset, en, reset
  and and_11 (and_11_out, D3_q, D2_q, D1_q);
  LED led_1 (.in(and_11_out));
endmodule
