// Logisim project Tn.circ as structural Verilog: 2 circuits, main circuit shit
module main (
  input  x,
  input  y1,
  input  y2,
  input  y3,
  output z,
  output D1,
  output D2,
  output D3
);

  wire and_1_out, and_2_out, and_3_out, and_4_out, and_5_out, and_6_out, and_7_out, and_9_out, and_10_out,
       and_11_out, and_12_out, and_13_out, and_14_out, and_15_out, not_1_out, not_2_out, not_3_out,
       not_4_out, not_5_out, not_6_out, not_7_out, not_8_out, not_9_out, not_10_out, not_11_out, not_12_out,
       not_13_out, not_14_out, or_2_out;

  and and_1 (and_1_out, y1, y2);
  not not_1 (not_1_out, y3);
  and and_2 (and_2_out, x, not_2_out);
  not not_2 (not_2_out, y1);
  not not_3 (not_3_out, y3);
  not not_4 (not_4_out, x);
  and and_3 (and_3_out, not_4_out, y1);
  not not_5 (not_5_out, y2);
  not not_6 (not_6_out, y1);
  and and_4 (and_4_out, not_6_out, not_7_out);
  not not_7 (not_7_out, y3);
  not not_8 (not_8_out, y2);
  and and_5 (and_5_out, x, y1);
  not not_9 (not_9_out, y2);
  not not_10 (not_10_out, x);
  and and_6 (and_6_out, not_10_out, not_11_out);
  not not_11 (not_11_out, y1);
  and and_7 (and_7_out, y2, not_12_out);
  not not_12 (not_12_out, y3);
  and and_8 (z, and_1_out, not_1_out);
  and and_9 (and_9_out, and_2_out, not_3_out);
  and and_10 (and_10_out, and_3_out, not_5_out);
  and and_11 (and_11_out, and_4_out, y2);
  and and_12 (and_12_out, y1, not_8_out);
  not not_13 (not_13_out, x);
  not not_14 (not_14_out, y2);
  and and_13 (and_13_out, and_5_out, not_9_out);
  and and_14 (and_14_out, and_6_out, and_7_out);
  or or_1 (D1, and_9_out, and_10_out);
  or or_2 (or_2_out, and_11_out, and_12_out);
  and and_15 (and_15_out, not_13_out, not_14_out);
  or or_3 (D3, and_13_out, and_14_out);
  or or_4 (D2, or_2_out, and_15_out);
endmodule

module shit (
  input  in_1,
  output out_2
);

  wire clock_1_out, d_ff_1_q, d_ff_2_q, d_ff_3_q, main_1_d1, main_1_d2, main_1_d3;

  main main_1 (
    .x(in_1), .y1(d_ff_1_q), .y2(d_ff_2_q), .y3(d_ff_3_q), .z(out_2), .D1(main_1_d1), .D2(main_1_d2),
    .D3(main_1_d3));
  Clock clock_1 (.out(clock_1_out));
  D_Flip_Flop d_ff_1 (.clk(clock_1_out), .D(main_1_d1), .Q(d_ff_1_q));  // open: Qn, preset, en, reset
  D_Flip_Flop d_ff_2 (.clk(clock_1_out), .D(main_1_d2), .Q(d_ff_2_q));  // open: Qn, preset, en, reset
  D_Flip_Flop d_ff_3 (.clk(clock_1_out), .D(main_1_d3), .Q(d_ff_3_q));  // open: Qn, preset, en, reset
endmodule
